# Fritzing sketch cw_knob_wiring (saved by Fritzing 0.9.0b)
breadboards: 1

parts:
  Potentiometer = Rotary Potentiometer (Small) [maximum_resistance=100kΩ package=THT]
  Uno = Arduino Uno (Rev3)
  LED1 = LED - 5mm [color="Red (633nm)" package="5 mm [THT]"]

nets:
  N1: Potentiometer.leg1, Uno.GND, LED1.cathode
  N2: Potentiometer.wiper, LED1.anode
  N3: Potentiometer.leg2, Uno.D13/SCK

notes:
  Clockwise-On Knob Wiring
